# Fritzing sketch Schéma de câblage (saved by Fritzing 0.9.3b)
breadboards: 1

parts:
  MKRFox1 = Arduino MKR Fox 1200
  Transfo = Voltage Regulator [package=78xxl]
  Transistor_NPN = NPN-Transistor [package="TO92 [THT]"]
  R1 = Resistor [tolerance=±5% resistance=10 package="1206 [SMD]"]
  R2 = Resistor [tolerance=±5% resistance=100k package="1206 [SMD]"]
  R3 = Resistor [tolerance=±5% resistance=150 package=THT]
  Bornier_CNPR = shrouded pin header, 6 pins [form="♂ (shrouded male)"]
  Piles_LS42 = Battery

nets:
  N1: MKRFox1.DAC0/A0, R3.Pin_0, Bornier_CNPR.pin2
  N2: MKRFox1.7, R1.Pin_1, R2.Pin_0
  GND: MKRFox1.GND, Transfo.GND, Transistor_NPN.E, R2.Pin_1, R3.Pin_1, Piles_LS42.-
  N3: MKRFox1.VIN, Transfo.OUT
  N4: Transfo.IN, Bornier_CNPR.pin1, Piles_LS42.+
  N5: Transistor_NPN.B, R1.Pin_0
  N6: Transistor_NPN.C, Bornier_CNPR.pin3

notes:
  Blanc
  Marron
  Jaune-Vert
